# Fritzing sketch camera_max3100 (saved by Fritzing 0.9.9b)
breadboards: 1

parts:
  RPi = Raspberry Pi Zero
  CAMERA = uCAM III
  S1 = Pushbutton [package="[THT]"]
  MAX3100_DIP = IC, DIP package, 14 pins [chip_label=IC]
  C1 = Ceramic Capacitor [capacitance=33pF voltage=35V package="100 mil [THT, multilayer]"]
  Crystal = CRYSTAL [package=tc26h]
  C4 = Ceramic Capacitor [capacitance=0.1µF voltage=35V package="100 mil [THT, multilayer]"]
  R3 = Resistor [tolerance=±5% resistance=10k power=0.25 package=THT]
  R2 = Resistor [tolerance=±5% resistance=220 power=0.25 package=THT]
  C3 = Ceramic Capacitor [capacitance=33pF voltage=35V package="100 mil [THT, multilayer]"]

nets:
  3.3V: RPi.pin_1, RPi.pin_17, MAX3100_DIP.pin14, C4.1, R3.Pin_0, R2.Pin_0
  5V: RPi.pin_2, RPi.pin_4, CAMERA.+5V
  GND: RPi.pin_6, RPi.pin_14, CAMERA.GND, MAX3100_DIP.pin7, C1.0, C4.0, C3.1
  N1: RPi.pin_16, CAMERA.RST
  N2: RPi.pin_18, S1.Pin_1, S1.Pin_2
  N3: RPi.pin_19, MAX3100_DIP.pin1
  N4: RPi.pin_21, MAX3100_DIP.pin2
  N5: RPi.pin_23, MAX3100_DIP.pin3
  N6: RPi.pin_24, MAX3100_DIP.pin4
  N7: CAMERA.TX, MAX3100_DIP.pin12
  N8: CAMERA.RX, MAX3100_DIP.pin13
  N9: S1.Pin_3, S1.Pin_4, R2.Pin_1
  N10: MAX3100_DIP.pin6, R3.Pin_1
  N11: MAX3100_DIP.pin8, C1.1, Crystal.1
  N12: MAX3100_DIP.pin9, Crystal.2, C3.0
