# Fritzing sketch camera_serial (saved by Fritzing 0.9.4)
breadboards: 1

parts:
  RPi = Raspberry Pi Zero
  CAMERA = uCAM III
  S1 = Pushbutton [package="[THT]"]
  R2 = Resistor [tolerance=±5% resistance=220 package=THT]

nets:
  3.3V: RPi.pin_1, RPi.pin_17, S1.Pin_1, S1.Pin_2
  5V: RPi.pin_2, RPi.pin_4, CAMERA.+5V
  GND: RPi.pin_6, RPi.pin_20, CAMERA.GND
  N1: RPi.pin_8, CAMERA.RX
  N2: RPi.pin_10, CAMERA.TX
  N3: RPi.pin_16, CAMERA.RST
  N4: RPi.pin_18, R2.Pin_0
  N5: S1.Pin_3, R2.Pin_1
